// Logisim project canvas6.circ as structural Verilog: 1 circuit, main circuit main
module main (
  input  A,
  input  B,
  input  C,
  output X,
  output Y
);

  wire _011_out, _101_out;

  not not_1 (X, A);
  and _011 (_011_out, ~A, B, C);  // AND_Gate
  or or_1 (Y, _011_out, _101_out);
  and _101 (_101_out, A, ~B, C);  // AND_Gate
endmodule
