// Logisim project canvas7.circ as structural Verilog: 1 circuit, main circuit main
module main (
  input  A,
  input  B,
  output C
);

  wire transistor_1_out, transistor_2_out, transistor_3_out, transistor_5_out;

  Transistor #(.\type ("n")) transistor_1 (.in(1'b1), .out(transistor_1_out), .gate(A));
  Transistor #(.\type ("n")) transistor_2 (.in(1'b1), .out(transistor_2_out), .gate(B));
  Transistor transistor_3 (.in(1'b0), .out(transistor_3_out), .gate(B));
  Transistor transistor_4 (.in(transistor_3_out), .out(C), .gate(A));
  Transistor #(.\type ("n")) transistor_5 (.in(1'b0), .out(transistor_5_out), .gate(A));
  Transistor #(.\type ("n")) transistor_6 (.in(transistor_5_out), .out(C), .gate(B));
  Transistor transistor_7 (.in(transistor_2_out), .out(C), .gate(A));
  Transistor transistor_8 (.in(transistor_1_out), .out(C), .gate(B));
endmodule
