// Logisim project multiplexer.circ as structural Verilog: 1 circuit, main circuit main
module main (
  input  S1,
  input  S0,
  input  A,
  input  B,
  input  C,
  input  D,
  output Out
);

  wire _00_out, _01_out, _10_out, _11_out;

  and _00 (_00_out, A, ~S1, ~S0);  // AND_Gate
  and _01 (_01_out, B, ~S1, S0);  // AND_Gate
  and _10 (_10_out, C, S1, S1, ~S0);  // AND_Gate
  and _11 (_11_out, D, S1, S0);
  or or_1 (Out, _00_out, _01_out, _10_out, _11_out);
endmodule
