// Logisim project H3.circ as structural Verilog: 1 circuit, main circuit main
module main (
  input  Clock,
  input  Input,
  input  Preset,
  input  Clear,
  output Output
);

  wire and_1_out, and_2_out, and_3_out, and_4_out, and_5_out, and_6_out, and_7_out, not_1_out, or_1_out,
       or_2_out, State_0_q, State_1_q, State_2_q, State_3_q, State_4_q;

  not not_1 (not_1_out, Input);
  and and_1 (and_1_out, not_1_out, State_0_q);
  or or_1 (or_1_out, and_2_out, and_1_out);
  D_Flip_Flop State_0 (.clk(Clock), .D(or_1_out), .Q(State_0_q), .preset(Preset), .reset(Clear));  // open: Qn, en
  and and_2 (and_2_out, State_4_q, not_1_out);
  and and_3 (and_3_out, State_3_q, not_1_out);
  and and_4 (and_4_out, State_2_q, not_1_out);
  and and_5 (and_5_out, State_1_q, not_1_out);
  or or_2 (or_2_out, State_0_q, State_1_q, State_2_q, State_3_q, State_4_q);
  and and_6 (and_6_out, or_2_out, Input);
  D_Flip_Flop d_ff_1 (.clk(Clock), .D(and_7_out), .Q(Output));  // open: Qn, preset, en, reset
  and and_7 (and_7_out, State_4_q, Input);
  D_Flip_Flop State_2 (.clk(Clock), .D(and_5_out), .Q(State_2_q), .reset(Clear));  // open: Qn, preset, en
  D_Flip_Flop State_1 (.clk(Clock), .D(and_6_out), .Q(State_1_q), .reset(Clear));  // open: Qn, preset, en
  D_Flip_Flop State_3 (.clk(Clock), .D(and_4_out), .Q(State_3_q), .reset(Clear));  // open: Qn, preset, en
  D_Flip_Flop State_4 (.clk(Clock), .D(and_3_out), .Q(State_4_q), .reset(Clear));  // open: Qn, preset, en
endmodule
