// Logisim project multiplexer.circ as structural Verilog: 1 circuit, main circuit main
module main (
  input  A,
  input  B,
  output W,
  output X,
  output Y,
  output Z
);

  and and_1 (W, ~A, ~B);  // AND_Gate
  and and_2 (X, ~A, B);  // AND_Gate
  and and_3 (Y, A, ~B);  // AND_Gate
  and and_4 (Z, A, B);
endmodule
