// Logisim project and.circ as structural Verilog: 1 circuit, main circuit main
module main (
  input  A,
  input  B,
  output O
);

  wire transistor_1_out;

  Transistor #(.\type ("n")) transistor_1 (.in(1'b1), .out(transistor_1_out), .gate(B));
  Transistor transistor_2 (.in(1'b0), .out(O), .gate(B));
  Transistor #(.\type ("n")) transistor_3 (.in(transistor_1_out), .out(O), .gate(A));
  Transistor transistor_4 (.in(1'b0), .out(O), .gate(A));
endmodule
