// Logisim project bool.circ as structural Verilog: 1 circuit, main circuit main
module main (
  input  A,
  input  B,
  input  C,
  output X,
  output Y
);

  wire A_nB_out, ABC_out, nA_nB_out;

  and nA_nB (nA_nB_out, ~A, ~B);  // AND_Gate
  and A_nB (A_nB_out, A, ~B);  // AND_Gate
  and ABC (ABC_out, B, A, C);
  or or_1 (X, A_nB_out, nA_nB_out, ABC_out);
  or or_2 (Y, nA_nB_out, B);
endmodule
