// Logisim project latch.circ as structural Verilog: 1 circuit, main circuit main
module main (
  input  SET,
  input  RESET,
  output Q,
  output nQ
);

  nand nand_1 (Q, SET, nQ);
  nand nand_2 (nQ, Q, RESET);
endmodule
