// Logisim project HW3.circ as structural Verilog: 1 circuit, main circuit main
module main (
  input  Input,
  input  Preset,
  input  Reset,
  output Output
);

  wire and_1_out, and_2_out, and_3_out, and_4_out, and_5_out, and_6_out, and_7_out, and_8_out, and_9_out,
       and_10_out, Clock_out, not_1_out, or_1_out, or_2_out, State_0_q, State_1_q, State_2_q, State_3_q,
       State_4_q;

  Clock Clock (.out(Clock_out));
  not not_1 (not_1_out, Input);
  and and_1 (and_1_out, State_4_q, not_1_out);
  and and_2 (and_2_out, State_0_q, not_1_out);
  D_Flip_Flop State_0 (.clk(Clock_out), .D(or_1_out), .Q(State_0_q), .preset(Preset), .reset(Reset));  // open: Qn, en
  or or_1 (or_1_out, and_1_out, and_2_out);
  and and_3 (and_3_out, Input, State_0_q);
  and and_4 (and_4_out, Input, State_1_q);
  and and_5 (and_5_out, Input, State_2_q);
  and and_6 (and_6_out, Input, State_3_q);
  and and_7 (and_7_out, Input, State_4_q);
  or or_2 (or_2_out, and_3_out, and_4_out, and_5_out, and_6_out, and_7_out);
  D_Flip_Flop State_1 (.clk(Clock_out), .D(or_2_out), .Q(State_1_q), .reset(Reset));  // open: Qn, preset, en
  and and_8 (and_8_out, State_1_q, not_1_out);
  D_Flip_Flop Output_Latch (.clk(Clock_out), .D(and_7_out), .Q(Output));  // open: Qn, preset, en, reset
  D_Flip_Flop State_2 (.clk(Clock_out), .D(and_8_out), .Q(State_2_q), .reset(Reset));  // open: Qn, preset, en
  D_Flip_Flop State_3 (.clk(Clock_out), .D(and_9_out), .Q(State_3_q), .reset(Reset));  // open: Qn, preset, en
  and and_9 (and_9_out, State_2_q, not_1_out);
  and and_10 (and_10_out, State_3_q, not_1_out);
  D_Flip_Flop State_4 (.clk(Clock_out), .D(and_10_out), .Q(State_4_q), .reset(Reset));  // open: Qn, preset, en
endmodule
