// Logisim project r4.circ as structural Verilog: 1 circuit, main circuit main
module main (
  input  in_1,
  input  in_2,
  input  in_3,
  output out_4,
  output out_5
);

  wire and_1_out, or_1_out, xor_1_out;

  and and_1 (and_1_out, in_1, in_1, in_2);
  or or_1 (or_1_out, in_2, in_3);
  not not_1 (out_5, or_1_out);
  xor xor_1 (xor_1_out, and_1_out, out_5);
  not not_2 (out_4, xor_1_out);
endmodule
